// Logisim project ALU.circ as structural Verilog: 1 circuit, main circuit main
module main (
  input  [3:0] A,
  input  [3:0] B,
  input  CIN,
  input  [3:0] E,
  input  in_5,
  output [3:0] C,
  output COUT
);

  wire adder_1_cout;
  wire [3:0] adder_1_out;

  Adder #(.width(4)) adder_1 (.a(A), .b(B), .out(adder_1_out), .cin(CIN), .cout(adder_1_cout));
  assign C = adder_1_out & E;  // AND_Gate and_1, 4 bits wide
  and and_2 (COUT, adder_1_cout, in_5);
endmodule
